// Logisim project canonical_suite.circ as structural Verilog: 5 circuits, main circuit main
module main (
  input  A0,
  input  A1,
  input  E,
  output Y0,
  output Y1,
  output Y2,
  output Y3
);

  wire not_1_out, not_2_out;

  not not_1 (not_1_out, A0);
  not not_2 (not_2_out, A1);
  and and_1 (Y0, not_2_out, not_1_out, E);
  and and_2 (Y1, not_2_out, A0, E);
  and and_3 (Y2, A1, not_1_out, E);
  and and_4 (Y3, A1, A0, E);
endmodule

module \Классический_8_в_3  (
  input  X0,
  input  X1,
  input  X2,
  input  X3,
  input  X4,
  input  X5,
  input  X6,
  input  X7__7,
  output Y2__4,
  output Y1__2,
  output Y0__1
);

  or or_1 (Y2__4, X4, X5, X6, X7__7);
  or or_2 (Y1__2, X2, X3, X6, X7__7);
  or or_3 (Y0__1, X1, X3, X5, X7__7);

  // Notes on the sheet:
  //   Классический шифратор 8 в 3
endmodule

module \Мультиплексор_4_в_1  (
  input  D0,
  input  D1,
  input  D2,
  input  D3,
  input  A0,
  input  A1,
  input  E,
  output Y
);

  wire and_1_out, and_2_out, and_3_out, and_4_out, not_1_out, not_2_out;

  not not_1 (not_1_out, A0);
  not not_2 (not_2_out, A1);
  and and_1 (and_1_out, D0, not_2_out, not_1_out, E);
  and and_2 (and_2_out, D1, not_2_out, A0, E);
  and and_3 (and_3_out, D2, A1, not_1_out, E);
  and and_4 (and_4_out, D3, A1, A0, E);
  or or_1 (Y, and_1_out, and_2_out, and_3_out, and_4_out);
endmodule

module \Демультиплексор_1_в_4  (
  input  DI,
  input  E,
  input  A0,
  input  A1,
  output Y0,
  output Y1,
  output Y2,
  output Y3
);

  wire not_1_out, not_2_out;

  not not_1 (not_1_out, A0);
  not not_2 (not_2_out, A1);
  and and_1 (Y0, DI, not_2_out, not_1_out, E);
  and and_2 (Y1, DI, not_2_out, A0, E);
  and and_3 (Y2, DI, A1, not_1_out, E);
  and and_4 (Y3, DI, A1, A0, E);
endmodule

module \Шифратор_20_в_5  (
  input  X0,
  input  X1,
  input  X2,
  input  X3,
  input  X4,
  input  X5,
  input  X6,
  input  X7,
  input  X8,
  input  X9,
  input  X10,
  input  X11,
  input  X12,
  input  X13,
  input  X14,
  input  X15,
  input  X16,
  input  X17,
  input  X18,
  input  X19__19,
  output Y4__16,
  output Y3__8,
  output Y2__4,
  output Y1__2,
  output Y0__1
);

  or or_1 (Y4__16, X16, X17, X18, X19__19);
  or or_2 (Y3__8, X8, X9, X10, X11, X12, X13, X14, X15);
  or or_3 (Y2__4, X4, X5, X6, X7, X12, X13, X14, X15);
  or or_4 (Y1__2, X2, X3, X6, X7, X10, X11, X14, X15, X18, X19__19);
  or or_5 (Y0__1, X1, X3, X5, X7, X9, X11, X13, X15, X17, X19__19);
endmodule
